// Logisim project a_cpu.circ as structural Verilog: 7 circuits, main circuit register_file
module register_file (
  input  [7:0] data_write,
  input  clear,
  input  write_enable,
  input  [1:0] read_reg,
  input  [1:0] write_reg,
  input  clk,
  input  reset,
  output [7:0] data_read
);

  wire and_1_out, and_2_out, and_3_out, and_4_out, decoder_1_out0, decoder_1_out1, decoder_1_out2,
       decoder_1_out3;
  wire [7:0] multiplexer_1_out, r0_q, r1_q, r2_q, r3_q;

  Multiplexer #(.width(8)) multiplexer_1 (.in0(data_write), .in1({8{1'b0}}), .out(multiplexer_1_out), .sel(clear));
  Decoder #(.enable("false"), .select(2)) decoder_1 (
    .out0(decoder_1_out0), .out1(decoder_1_out1), .out2(decoder_1_out2), .out3(decoder_1_out3),
    .sel(write_reg));
  Register r0 (.D(multiplexer_1_out), .en(and_1_out), .clk(clk), .Q(r0_q), .clr(reset));
  and and_1 (and_1_out, decoder_1_out0, write_enable);
  Register r1 (.D(multiplexer_1_out), .en(and_2_out), .clk(clk), .Q(r1_q), .clr(reset));
  and and_2 (and_2_out, decoder_1_out1, write_enable);
  Register r2 (.D(multiplexer_1_out), .en(and_3_out), .clk(clk), .Q(r2_q), .clr(reset));
  and and_3 (and_3_out, decoder_1_out2, write_enable);
  Register r3 (.D(multiplexer_1_out), .en(and_4_out), .clk(clk), .Q(r3_q), .clr(reset));
  and and_4 (and_4_out, decoder_1_out3, write_enable);
  Multiplexer #(.select(2), .width(8)) multiplexer_2 (
    .in0(r0_q), .in1(r1_q), .in2(r2_q), .in3(r3_q), .out(data_read), .sel(read_reg));
endmodule

module alu (
  input  [7:0] A,
  input  [7:0] B,
  input  op,
  output [7:0] data_out
);

  wire [7:0] adder_1_out, and_1_out;

  Adder adder_1 (.a(A), .b(B), .out(adder_1_out));  // open: cin, cout
  assign and_1_out = B & A;  // AND_Gate and_1, 8 bits wide
  Multiplexer #(.width(8)) multiplexer_1 (.in0(adder_1_out), .in1(and_1_out), .out(data_out), .sel(op));
endmodule

module instr_decoder (
  input  [7:0] instr,
  output [1:0] imm,
  output [1:0] read_reg,
  output [1:0] write_reg,
  output write_en,
  output alu_op,
  output reg_clear
);

  ophandle ophandle_1 (.Opcode(instr[7:6]), .write_en(write_en), .alu_op(alu_op), .reg_clear(reg_clear));

  assign imm = instr[1:0];
  assign read_reg = instr[3:2];
  assign write_reg = instr[5:4];
endmodule

module ophandle (
  input  [1:0] Opcode,
  output write_en,
  output alu_op,
  output reg_clear
);

  not not_1 (alu_op, Opcode[0]);
  or or_1 (write_en, Opcode[0], Opcode[1]);
  and and_1 (reg_clear, Opcode[1], Opcode[0]);
endmodule

module cpu (
  input  [7:0] Instr,
  input  Clk,
  input  Reset,
  output [7:0] MemBus,
  output [7:0] data_out
);

  wire controller_1_aluoutsel, controller_1_asel, controller_1_bsel, instr_decoder_1_alu_op,
       instr_decoder_1_reg_clear, instr_decoder_1_write_en, multiplexer_1_out, multiplexer_4_out;
  wire [1:0] instr_decoder_1_imm, instr_decoder_1_read_reg, instr_decoder_1_write_reg;
  wire [7:0] alu_1_data_out, bit_extender_1_out, demultiplexer_1_out0, demultiplexer_1_out1,
       multiplexer_2_out, multiplexer_3_out;

  Register PC (.D(demultiplexer_1_out1), .en(controller_1_aluoutsel), .clk(Clk), .Q(MemBus), .clr(Reset));
  instr_decoder instr_decoder_1 (
    .instr(Instr), .imm(instr_decoder_1_imm), .read_reg(instr_decoder_1_read_reg),
    .write_reg(instr_decoder_1_write_reg), .write_en(instr_decoder_1_write_en),
    .alu_op(instr_decoder_1_alu_op), .reg_clear(instr_decoder_1_reg_clear));
  assign bit_extender_1_out = {{6{1'b0}}, instr_decoder_1_imm};  // Bit_Extender bit_extender_1
  register_file register_file_1 (
    .data_write(demultiplexer_1_out0), .clear(instr_decoder_1_reg_clear), .write_enable(multiplexer_1_out),
    .read_reg(instr_decoder_1_read_reg), .write_reg(instr_decoder_1_write_reg), .clk(Clk), .reset(Reset),
    .data_read(data_out));
  Multiplexer multiplexer_1 (
    .in0(instr_decoder_1_write_en), .in1(1'b0), .out(multiplexer_1_out), .sel(controller_1_asel));
  controller controller_1 (
    .Clk(Clk), .Reset(Reset), .Asel(controller_1_asel), .Bsel(controller_1_bsel),
    .ALUOutSel(controller_1_aluoutsel));
  Multiplexer #(.width(8)) multiplexer_2 (
    .in0(bit_extender_1_out), .in1(MemBus), .out(multiplexer_2_out), .sel(controller_1_asel));
  Multiplexer #(.width(8)) multiplexer_3 (.in0(data_out), .in1(8'h1), .out(multiplexer_3_out), .sel(controller_1_bsel));
  Multiplexer multiplexer_4 (
    .in0(instr_decoder_1_alu_op), .in1(1'b0), .out(multiplexer_4_out), .sel(controller_1_asel));
  Demultiplexer #(.width(8)) demultiplexer_1 (
    .out0(demultiplexer_1_out0), .out1(demultiplexer_1_out1), .in(alu_1_data_out),
    .sel(controller_1_aluoutsel));
  alu alu_1 (.A(multiplexer_2_out), .B(multiplexer_3_out), .op(multiplexer_4_out), .data_out(alu_1_data_out));
endmodule

module main (
  output [7:0] out_1,
  output [7:0] out_2,
  output [7:0] out_3
);

  wire button_1_out, button_2_out;

  Button button_1 (.out(button_1_out));
  Button button_2 (.out(button_2_out));
  ROM rom_1 (.addr(out_3), .data(out_2));
  cpu cpu_1 (.Instr(out_2), .Clk(button_1_out), .Reset(button_2_out), .MemBus(out_3), .data_out(out_1));
  Hex_Digit_Display hex_digit_display_1 (.value(out_1[7:4]));  // open: dp
  Hex_Digit_Display hex_digit_display_2 (.value(out_1[3:0]));  // open: dp

  // Notes on the sheet:
  //   contents of rom_1 (hex, n*v repeats v):
  //   41 56 6b 7f 7d
endmodule

module controller (
  input  Clk,
  input  Reset,
  output Asel,
  output Bsel,
  output ALUOutSel
);

  T_Flip_Flop t_ff_1 (.T(Clk), .clk(Clk), .Q(ALUOutSel), .reset(Reset));  // open: Qn, preset

  assign Asel = ALUOutSel;
  assign Bsel = ALUOutSel;
endmodule
